# Fritzing sketch LED RGB Strip Controller (saved by Fritzing 0.9.4)
breadboards: 1

parts:
  Q2 = Basic FET N-Channel [package="D2Pak [SMD]"]
  Q3 = Basic FET N-Channel [package="D2Pak [SMD]"]
  Q1 = Basic FET N-Channel [package="D2Pak [SMD]"]
  WeMos_D1_Mini1 = WeMos D1 Mini
  12v_In_5v_Out = Mini-360 DC-DC Buck converter [package=THT]
  RGB_Strip_LED1 = RGB Strip LED
  12v = Power plug

nets:
  N1: Q2.Gate, WeMos_D1_Mini1.D8
  N2: Q2.drain, RGB_Strip_LED1.Red_Connect
  N3: Q2.source, Q3.source, Q1.source, WeMos_D1_Mini1.5V, WeMos_D1_Mini1.G
  N4: Q3.Gate, WeMos_D1_Mini1.D6
  N5: Q3.drain, RGB_Strip_LED1.Blue_Connect
  N6: Q1.Gate, WeMos_D1_Mini1.D7
  N7: Q1.drain, RGB_Strip_LED1.Green_Connect
  N8: 12v_In_5v_Out.IN-, 12v.GND
  N9: 12v_In_5v_Out.IN+, RGB_Strip_LED1.Common_Connect, 12v.VCC
  N10: 12v_In_5v_Out.OUT+, 12v_In_5v_Out.OUT-

custom parts:
  Mini-360 DC-DC Buck converter: Mini-360 DC-DC Buck converter. Tiny buck step down voltage converter, input voltage 4.75 to 23V output 1 to 17V adjustable. Available from ebay and the like.
  RGB Strip LED: A tri-color Strip LED with red, green and blue. Based on LED SMD 5050 RGB Pin order: common cathode - green - red - blue
